# Fritzing sketch Show_Love_In_A_Heartbeat_Rev2 (saved by Fritzing 0.7.4b)
breadboards: 1

parts:
  R1 = Resistor [tolerance=±5% resistance=100k package=THT]
  R2 = Resistor [tolerance=±5% resistance=100k package=THT]
  LED1 = LED - 5mm [color="Red (633nm)" package="5 mm [THT]"]
  R3 = Resistor [tolerance=±5% resistance=470 package=THT]
  R4 = Resistor [tolerance=±5% resistance=470 package=THT]
  C1 = Electrolytic Capacitor [capacitance=0.1mF package="100 mil [THT, electrolytic]"]
  C2 = Electrolytic Capacitor [capacitance=0.1mF package="100 mil [THT, electrolytic]"]
  Q1 = NPN-Transistor [package="TO92 [THT]"]
  Q2 = NPN-Transistor [package="TO92 [THT]"]
  VCC = Battery
  PCB1 = Custom PCB - HeartPCB2 - Mario  # not connected
  LED2 = LED - 5mm [color="Red (633nm)" package="5 mm [THT]"]

nets:
  N1: R1.Pin_0, C1.-, Q1.B
  N2: R1.Pin_1, R2.Pin_1, LED1.anode, VCC.+, LED2.anode
  N3: R2.Pin_0, C2.-, Q2.B
  N4: LED1.cathode, R4.Pin_1
  N5: R3.Pin_0, LED2.cathode
  N6: R3.Pin_1, C2.+, Q1.C
  N7: R4.Pin_0, C1.+, Q2.C
  N8: Q1.E, Q2.E, VCC.-

notes:
  Rev. 2
  Heartbeat
  Dev-O-Rama

custom parts:
  Custom PCB - HeartPCB2 - Mario: Custom HeartPCB2 - Mario - 45.001x45.6061mm Circuit Board 2012-06-03 13:14:06
